# Fritzing sketch ShyGuy (saved by Fritzing 0.9.4)

parts:
  Arduino_CNC_Shield_V3_00_1 = Arduino_CNC_V3.00
  M1 = Stepper Motor - Bipolar
  S1 = Tilt Switch [package=THT]
  LED1 = smd LED [color="Red (633nm)" package="1206 [SMD]"]
  R1 = Resistor [tolerance=±5% resistance=220 package="0805 [SMD]"]
  R2 = Resistor [tolerance=±5% resistance=220 package="0805 [SMD]"]
  LED2 = smd LED [color="Red (633nm)" package="1206 [SMD]"]
  JACK1 = 2.1mm Barrel Jack with Terminal Block

nets:
  N1: Arduino_CNC_Shield_V3_00_1.POWER_-, JACK1.NEG
  N2: Arduino_CNC_Shield_V3_00_1.POWER_+, JACK1.POS
  N3: Arduino_CNC_Shield_V3_00_1.X-MTR_'1', M1.A
  N4: Arduino_CNC_Shield_V3_00_1.X-MTR_'2', M1.C
  N5: Arduino_CNC_Shield_V3_00_1.X-MTR_'3', M1.B
  N6: Arduino_CNC_Shield_V3_00_1.X-MTR_'4', M1.D
  N7: Arduino_CNC_Shield_V3_00_1.End_Stops_Z+_(and_Z-)_/_SpnEn, S1.Pin_1
  N8: Arduino_CNC_Shield_V3_00_1.End_Stops_Z+_(Gnd), S1.Pin_2
  N9: Arduino_CNC_Shield_V3_00_1.End_Stops_Y+_(and_Y-), Arduino_CNC_Shield_V3_00_1.End_Stops_Y-_(Gnd), R2.Pin_0
  N10: Arduino_CNC_Shield_V3_00_1.End_Stops_Y+_(Gnd), LED1.cathode
  N11: Arduino_CNC_Shield_V3_00_1.End_Stops_X+_(and_X-), R1.Pin_0
  N12: Arduino_CNC_Shield_V3_00_1.End_Stops_X+_(Gnd), LED2.cathode
  N13: LED1.anode, R2.Pin_1
  N14: R1.Pin_1, LED2.anode

notes:
  12V DC
  Vibration Sensor
  Eye LEDs
  NEMA17 Stepper Motor

custom parts:
  Arduino_CNC_V3.00: Protoneer Arduino CNC Shield V3.00 If using Grbl V0.9: The “A” axis can not be used (yet). The “SCL” (Arduino A5) pin is now used for 'Probing' input. The “End Stops Z+ & Z-” (Arduino D11) and “SpnEn” (Arduino D12) have been switched!
